# Fritzing sketch servo motor (saved by Fritzing 0.9.3b)
breadboards: 1

parts:
  BAT2 = Battery Holders [package=battery-aa]
  BAT3 = Battery Holders [package=battery-aa]
  BAT4 = Battery Holders [package=battery-aa]
  BAT1 = Battery Holders [package=battery-aa]
  J1 = Basic Servo
  J2 = Basic Servo
  부품1 = Arduino Uno (Rev3)
  R1 = Resistor [tolerance=±5% resistance=150 package=THT]
  R2 = Resistor [tolerance=±5% resistance=150 package=THT]

nets:
  N1: BAT2.-, BAT1.+
  N2: BAT2.+, BAT3.-
  N3: BAT3.+, R1.Pin_1
  N4: BAT4.-, R2.Pin_1
  N5: BAT4.+, BAT1.-
  GND: J1.gnd, J2.gnd, R1.Pin_0
  N6: J1.vcc, R2.Pin_0
  N7: J1.pulse, 부품1.D8
